# Fritzing sketch DavayLoRa_BSF_RX1 (saved by Fritzing 0.9.4)

parts:
  BSFrance_LoRa32u4 = Adafruit Feather 32u4 RFM9xW LoRa [part_number="Adafruit #3078 and Adafruit #3079"]
  U2 = Chip antenna [package=antenna-chip3]
  Main_Power_Switch = Toggle Switch [package=THT]
  Buzzer = Vibration Motor
  Bipper = Buzzer 12mm [package=buzzer-ccv-kit]
  DIP3_SW1 = DIP3 Switch 3 Position [package=dipswitch-03]
  SMD_COB_LED1 = RGB SMD COB LED 10x60 [package="5 mm [THT]"]
  Battery1 = LIPO-1000mAh [package=lipo-1000]
  MOSFET-1_60NO3 = MOSFET-NCHANNEL [package=to220v]
  MOSFET-2_60NO3 = MOSFET-NCHANNEL [package=to220v]
  SMD_COB_LED2 = RGB SMD COB LED 10x60 [package="5 mm [THT]"]

nets:
  N1: BSFrance_LoRa32u4.ANT, U2.SIGNAL
  GND: BSFrance_LoRa32u4.GND, Battery1.-, MOSFET-1_60NO3.S, MOSFET-2_60NO3.S
  N2: BSFrance_LoRa32u4.VBAT, Main_Power_Switch.COM, DIP3_SW1.4, DIP3_SW1.5, DIP3_SW1.6
  N3: BSFrance_LoRa32u4.6, BSFrance_LoRa32u4.3, MOSFET-1_60NO3.G
  N4: BSFrance_LoRa32u4.5, BSFrance_LoRa32u4.2, MOSFET-2_60NO3.G
  N5: Main_Power_Switch.L2, Battery1.+
  N6: Buzzer.POS, DIP3_SW1.3
  N7: Buzzer.NEG, Bipper.2, MOSFET-2_60NO3.D
  N8: Bipper.1, DIP3_SW1.2
  N9: DIP3_SW1.1, SMD_COB_LED1.red_anode, SMD_COB_LED2.red_anode
  N10: SMD_COB_LED1.common_cathode, MOSFET-1_60NO3.D, SMD_COB_LED2.common_cathode, SMD_COB_LED2.blue_anode

notes:
  Батарея на самом деле присоединяется к своему разъёму, а на плате перерезается дорожка между батареей и BAT
  Cut the board connector from Battery to VBAT and insert switch

custom parts:
  Adafruit Feather 32u4 RFM9xW LoRa: This is the Adafruit Feather 32u4 LoRa Radio (RFM9x) - our take on an microcontroller with a "Long Range (LoRa)" packet radio transceiver with built in USB and battery charging. Its an Adafruit Feather 32u4 with a 868/915 MHz radio module cooked in! Great for making wireless networks that can go further than 2.4GHz 802.15.4 and similar, are more flexible than Bluetooth LE and without the high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
  Vibration Motor: An eccentric vibration motor!
  DIP3 Switch 3 Position: DIP Switch 3
  RGB SMD COB LED 10x60: A 10x60 tri-color LED with red, green and blue inside.
