# Fritzing sketch DavayLoRa_BSF_TX1 (saved by Fritzing 0.9.4)

parts:
  BSFrance_LoRa32u4 = Adafruit Feather 32u4 RFM9xW LoRa [part_number="Adafruit #3078 and Adafruit #3079"]
  Antenna = Chip antenna [package=antenna-chip3]
  ON/OFF_Switch = Toggle Switch [package=THT]
  Battery = LIPO-1000mAh [package=lipo-1000]
  MOSFET_60NO3 = MOSFET-NCHANNEL [package=to220v]
  Main_LED = RGB SMD COB LED 10x60 [package="5 mm [THT]"]
  MAIN_PUSHBUTTON_With_FB_LED = Waterproof Pushbutton (red)
  R1 = Resistor [tolerance=±5% resistance=100k package=THT]
  R2 = Resistor [tolerance=±5% resistance=100k package=THT]

nets:
  N1: BSFrance_LoRa32u4.ANT, Antenna.SIGNAL
  N2: BSFrance_LoRa32u4.A1, R1.Pin_0, R2.Pin_0
  GND: BSFrance_LoRa32u4.GND, Battery.-, MOSFET_60NO3.S, MAIN_PUSHBUTTON_With_FB_LED.NO#2, MAIN_PUSHBUTTON_With_FB_LED.-_LED, R1.Pin_1
  N3: BSFrance_LoRa32u4.VBAT, ON/OFF_Switch.COM, Main_LED.red_anode, R2.Pin_1
  N4: BSFrance_LoRa32u4.11, MOSFET_60NO3.G
  N5: BSFrance_LoRa32u4.6, MAIN_PUSHBUTTON_With_FB_LED.NO#1
  N6: BSFrance_LoRa32u4.5, MAIN_PUSHBUTTON_With_FB_LED.+_LED
  N7: ON/OFF_Switch.L2, Battery.+
  N8: MOSFET_60NO3.D, Main_LED.common_cathode, Main_LED.green_anode

notes:
  Батарея присоединяется к своему разъёму, а на плате перерезается дорожка между батареей и BAT

custom parts:
  Adafruit Feather 32u4 RFM9xW LoRa: This is the Adafruit Feather 32u4 LoRa Radio (RFM9x) - our take on an microcontroller with a "Long Range (LoRa)" packet radio transceiver with built in USB and battery charging. Its an Adafruit Feather 32u4 with a 868/915 MHz radio module cooked in! Great for making wireless networks that can go further than 2.4GHz 802.15.4 and similar, are more flexible than Bluetooth LE and without the high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
  RGB SMD COB LED 10x60: A 10x60 tri-color LED with red, green and blue inside.
  Waterproof Pushbutton (red): Waterproof Illuminated ON Pushbutton (red)
