# Fritzing sketch DavayLoRa_HT_RX (saved by Fritzing 0.9.4)

parts:
  Battery1 = LIPO-1000mAh [package=lipo-1000]
  MOSFET1_60NO2 = MOSFET-NCHANNEL [package=to220v]
  Big_LED = RGB SMD COB LED 10x60 [package="5 mm [THT]"]
  Antenna1 = Chip antenna [package=antenna-chip3]  # not connected
  Mod1 = Heltec Wireless Stick Lite V3 [part_number=HTIT-WSL_V3]
  MOSFET2_60NO2 = MOSFET-NCHANNEL [package=to220v]
  Buzzer1 = Vibration Motor
  Reed_switch_NO = Reed switch [package=THT]

nets:
  N1: Battery1.+, Big_LED.red_anode, Buzzer1.POS
  GND: Battery1.-, MOSFET1_60NO2.S, MOSFET2_60NO2.S
  N2: MOSFET1_60NO2.G, Mod1.pin_34
  N3: MOSFET1_60NO2.D, Big_LED.common_cathode
  N4: Mod1.pin4, Reed_switch_NO.pin_1
  N5: Mod1.pin_18, Reed_switch_NO.pin_2
  N6: Mod1.pin_35, MOSFET2_60NO2.G
  N7: MOSFET2_60NO2.D, Buzzer1.NEG

custom parts:
  RGB SMD COB LED 10x60: A 10x60 tri-color LED with red, green and blue inside.
  Heltec Wireless Stick Lite V3: Wireless Stick Lite (Panda Board) is a part of the Heltec LoRa series and incorporates an ESP32-S3FN8 processor, WiFi, SX1262 LoRa and Bluetooth with an integrated CP2102 USB to serial port interface and onboard SHT1.25 battery interface with integrated lithium battery management system. Links: Heltec Wireless Stick Lite product page Github
  Vibration Motor: An eccentric vibration motor!
