# Fritzing sketch DavayLoRa_HT_TX (saved by Fritzing 0.9.4)

parts:
  Battery1 = LIPO-1000mAh [package=lipo-1000]
  MOSFET_60NO2 = MOSFET-NCHANNEL [package=to220v]
  MAIN_PUSHBUTTON_With_FB_LED1 = Waterproof Pushbutton (red)
  Big_LED = RGB SMD COB LED 10x60 [package="5 mm [THT]"]
  Antenna1 = Chip antenna [package=antenna-chip3]  # not connected
  Mod1 = Heltec Wireless Stick Lite V3 [part_number=HTIT-WSL_V3]

nets:
  N1: Battery1.+, Big_LED.red_anode
  GND: Battery1.-, MOSFET_60NO2.S, MAIN_PUSHBUTTON_With_FB_LED1.NO#2, MAIN_PUSHBUTTON_With_FB_LED1.-_LED
  N2: MOSFET_60NO2.G, Mod1.pin_34
  N3: MOSFET_60NO2.D, Big_LED.common_cathode
  N4: MAIN_PUSHBUTTON_With_FB_LED1.NO#1, Mod1.pin_36
  N5: MAIN_PUSHBUTTON_With_FB_LED1.+_LED, Mod1.pin_28

custom parts:
  Waterproof Pushbutton (red): Waterproof Illuminated ON Pushbutton (red)
  RGB SMD COB LED 10x60: A 10x60 tri-color LED with red, green and blue inside.
  Heltec Wireless Stick Lite V3: Wireless Stick Lite (Panda Board) is a part of the Heltec LoRa series and incorporates an ESP32-S3FN8 processor, WiFi, SX1262 LoRa and Bluetooth with an integrated CP2102 USB to serial port interface and onboard SHT1.25 battery interface with integrated lithium battery management system. Links: Heltec Wireless Stick Lite product page Github
